// Logisim project ALU_main.circ as structural Verilog
module main (
  input  A4,
  input  A3,
  input  A2,
  input  A1,
  input  B4,
  input  B3,
  input  B2,
  input  B1,
  input  CS0,
  input  CS1,
  input  CS2,
  output C,
  output V,
  output S,
  output Z,
  output O4,
  output O3,
  output O2,
  output O1
);

  wire A_y1, A_y2, A_y3, A_y4, adder_2__15__s4, B_y1, B_y2, B_y3, B_y4, n7404_1_p2, n7404_1_p4, n7404_1_p6,
       n7404_1_p8, n7404_1_p10, n7404_1_p12, n7404_2_p2, n7404_2_p4, n7404_2_p6, n7404_2_p8, n7404_2_p10,
       n7408_1_p3, n7408_1_p6, n7408_1_p9, n7408_1_p12, n7408_2_p3, n7408_2_p6, n7408_2_p8, n7408_2_p9,
       n7408_2_p12, n7432_1_p3, n7432_1_p6, n7432_1_p9, n7432_1_p12, n7432_2_p6, n7432_2_p9, n7432_2_p12;

  // _7404 7404_1: pin names not known; wires that end beside it: A1, n7404_1_p2, A2, n7404_1_p4, A3, n7404_1_p6, A4, n7404_1_p8, B4, n7404_1_p10, B3, n7404_1_p12
  // _7404 7404_2: pin names not known; wires that end beside it: B2, n7404_2_p2, B1, n7404_2_p4, CS0, n7404_2_p6, CS1, n7404_2_p8, CS2, n7404_2_p10
  // _7408 7408_1: pin names not known; wires that end beside it: B4, A4, n7408_1_p3, A3, B3, n7408_1_p6, A2, B2, n7408_1_p9, A1, B1, n7408_1_p12
  // _7432 7432_1: pin names not known; wires that end beside it: B4, A4, n7432_1_p3, A3, B3, n7432_1_p6, A2, B2, n7432_1_p9, B1, A1, n7432_1_p12
  // _7408 7408_2: pin names not known; wires that end beside it: n7404_2_p6, CS1, n7408_2_p3, n7404_2_p6, n7404_2_p10, n7408_2_p6, CS2, n7408_2_p8, n7408_2_p9, n7408_2_p6, n7404_2_p8, n7408_2_p12
  // _7432 7432_2: pin names not known; wires that end beside it: CS0, n7404_2_p8, n7408_2_p8, O1, O2, n7432_2_p6, O4, O3, n7432_2_p9, n7432_2_p9, n7432_2_p6, n7432_2_p12
  MUX A (
    ._001(A1), ._002(n7404_1_p2), ._003(n7432_1_p12), ._004(n7408_1_p12), ._011(A2), ._012(n7404_1_p4),
    ._013(n7432_1_p9), ._014(n7408_1_p9), ._101(A3), ._102(n7404_1_p6), ._103(n7432_1_p6), ._104(n7408_1_p6),
    ._111(A4), ._112(n7404_1_p8), ._113(n7432_1_p3), ._114(n7408_1_p3), .S1(n7408_2_p9), .S0(CS0), .Y1(A_y1),
    .Y2(A_y2), .Y3(A_y3), .Y4(A_y4));
  MUX B (
    ._001(1'b0), ._002(B1), ._003(1'b1), ._004(n7404_2_p4), ._011(1'b0), ._012(B2), ._013(1'b1),
    ._014(n7404_2_p2), ._101(1'b0), ._102(B3), ._103(1'b1), ._104(n7404_1_p12), ._111(1'b0), ._112(B4),
    ._113(1'b1), ._114(n7404_1_p10), .S1(n7408_2_p6), .S0(n7408_2_p3), .Y1(B_y1), .Y2(B_y2), .Y3(B_y3),
    .Y4(B_y4));
  Adder adder_1 (
    ._1__A4(1'b0), ._3__A3(1'b0), ._4__B3(1'b0), ._6__S2(C), ._7__B2(1'b0), ._8__A2(1'b0), ._16__B4(1'b0),
    ._13__Cin(adder_2__15__s4), ._11__B1(B_y4), ._10__A1(A_y4), ._9__S1(O4));  // open: _2__S3, _5__Vcc, _15__S4, _14__Cout, _12__GND
  Adder adder_2 (
    ._1__A4(1'b0), ._2__S3(O3), ._3__A3(A_y3), ._4__B3(B_y3), ._6__S2(O2), ._7__B2(B_y2), ._8__A2(A_y2),
    ._16__B4(1'b0), ._15__S4(adder_2__15__s4), ._13__Cin(n7408_2_p12), ._11__B1(B_y1), ._10__A1(A_y1),
    ._9__S1(O1));  // open: _5__Vcc, _14__Cout, _12__GND
  // _7486 7486_1: pin names not known; wires that end beside it: C, adder_2__15__s4, V, 1'b1, n7432_2_p12, Z

  assign S = O4;

  // Notes on the sheet:
  //   A'
  //   B', cs's
  //   A AND B
  //   A OR B
  //   cs1
  //   cin
endmodule

module Adder (
  input  _1__A4,
  input  _16__B4,
  input  _3__A3,
  input  _4__B3,
  input  _13__Cin,
  input  _5__Vcc,
  input  _12__GND,
  input  _11__B1,
  input  _7__B2,
  input  _10__A1,
  input  _8__A2,
  output _2__S3,
  output _15__S4,
  output _14__Cout,
  output _6__S2,
  output _9__S1
);

  wire and_1_out, and_2_out, and_3_out, and_4_out, and_5_out, and_6_out, and_7_out, and_8_out, and_9_out,
       and_10_out, and_11_out, and_12_out, and_13_out, and_14_out, nand_1_out, nand_2_out, nand_3_out,
       nand_4_out, nor_1_out, nor_2_out, nor_3_out, nor_4_out, nor_6_out, nor_7_out, nor_8_out, not_1_out,
       not_2_out, not_3_out, not_4_out, not_5_out, not_6_out;

  nand nand_1 (nand_1_out, _16__B4, _1__A4);
  nor nor_1 (nor_1_out, _16__B4, _1__A4);
  nand nand_2 (nand_2_out, _4__B3, _3__A3);
  nor nor_2 (nor_2_out, _4__B3, _3__A3);
  nand nand_3 (nand_3_out, _7__B2, _8__A2);
  nor nor_3 (nor_3_out, _7__B2, _8__A2);
  nand nand_4 (nand_4_out, _11__B1, _10__A1);
  nor nor_4 (nor_4_out, _11__B1, _10__A1);
  and and_1 (and_1_out, nor_2_out, nand_1_out);
  and and_2 (and_2_out, nor_3_out, nand_1_out, nand_2_out);
  and and_3 (and_3_out, nor_4_out, nand_1_out, nand_2_out, nand_3_out);
  and and_4 (and_4_out, nand_1_out, nand_2_out, nand_3_out, nand_4_out, not_2_out);
  not not_1 (not_1_out, nor_1_out);
  and and_5 (and_5_out, nor_3_out, nand_2_out);
  and and_6 (and_6_out, nor_4_out, nand_2_out, nand_3_out);
  and and_7 (and_7_out, nand_2_out, nand_3_out, nand_4_out, not_2_out);
  not not_2 (not_2_out, _13__Cin);
  not not_3 (not_3_out, nor_2_out);
  and and_8 (and_8_out, nor_4_out, nand_3_out);
  and and_9 (and_9_out, nand_3_out, nand_4_out, not_2_out);
  not not_4 (not_4_out, nor_3_out);
  and and_10 (and_10_out, nand_4_out, not_2_out);
  not not_5 (not_5_out, nor_4_out);
  not not_6 (not_6_out, not_2_out);
  nor nor_5 (_14__Cout, nor_1_out, and_1_out, and_2_out, and_3_out, and_4_out);
  and and_11 (and_11_out, nand_1_out, not_1_out);
  and and_12 (and_12_out, nand_2_out, not_3_out);
  and and_13 (and_13_out, nand_3_out, not_4_out);
  and and_14 (and_14_out, nand_4_out, not_5_out);
  xor xor_1 (_15__S4, and_11_out, nor_6_out);
  nor nor_6 (nor_6_out, nor_2_out, and_5_out, and_6_out, and_7_out);
  xor xor_2 (_2__S3, and_12_out, nor_7_out);
  nor nor_7 (nor_7_out, nor_3_out, and_8_out, and_9_out);
  xor xor_3 (_6__S2, and_13_out, nor_8_out);
  nor nor_8 (nor_8_out, nor_4_out, and_10_out);
  xor xor_4 (_9__S1, and_14_out, not_6_out);

  // Notes on the sheet:
  //   7483: 4-bit full adder
endmodule

module MUX (
  input  _001,
  input  _002,
  input  _003,
  input  _004,
  input  _011,
  input  _012,
  input  _013,
  input  _014,
  input  _101,
  input  _102,
  input  _103,
  input  _104,
  input  _111,
  input  _112,
  input  _113,
  input  _114,
  input  S1,
  input  S0,
  output Y1,
  output Y2,
  output Y3,
  output Y4
);

  // _74153 74153_1: pin names not known; wires that end beside it: Y2, Y1, _011, _001, _012, _002, _013, _003, _014, _004, S1, S0
  // _74153 74153_2: pin names not known; wires that end beside it: Y4, Y3, _111, _101, _112, _102, _113, _103, _114, _104, S1, S0
endmodule
