// Logisim project Comparator.circ as structural Verilog: 3 circuits, main circuit Comparator_With_Smaller_Fraction
// CMP_32
module Comparator_With_Smaller_Fraction (
  input  [31:0] X_fraction,
  input  [31:0] Y_fraction,
  input  [8:0] X,
  input  [8:0] Y,
  output [31:0] LargerFraction,
  output [31:0] SmallerFraction,
  output X_Y,
  output [8:0] Common_Exponent,
  output [4:0] Difference
);

  wire alu_12_bit_3_sign_flag;
  wire [11:0] alu_12_bit_1_output, alu_12_bit_2_output;
  wire [11:5] mux_12_bit_1_output;

  ALU_12_bit alu_12_bit_1 (
    .Input_1({3'b000, X}), .Input_2({3'b000, Y}), .Control(2'b11), .Output(alu_12_bit_1_output),
    .Sign_Flag(X_Y));  // open: Carry_Out, Zero_Flag
  MUX_32_bit mux_32_bit_1 (.X(Y_fraction), .Y(X_fraction), .Selection(X_Y), .Output(SmallerFraction));
  MUX_9_bit mux_9_bit_1 (.X(X), .Y(Y), .Selection(X_Y), .Output(Common_Exponent));
  ALU_12_bit alu_12_bit_2 (
    .Input_1(alu_12_bit_1_output), .Control({1'b0, X_Y}), .Output(alu_12_bit_2_output));  // open: Input_2, Carry_Out, Zero_Flag, Sign_Flag
  MUX_32_bit mux_32_bit_2 (.X(X_fraction), .Y(Y_fraction), .Selection(X_Y), .Output(LargerFraction));
  ALU_12_bit alu_12_bit_3 (
    .Input_1(alu_12_bit_2_output), .Input_2(12'h1f), .Control(2'b11), .Sign_Flag(alu_12_bit_3_sign_flag));  // open: Output, Carry_Out, Zero_Flag
  MUX_12_bit mux_12_bit_1 (
    .X(12'h1f), .Y(alu_12_bit_2_output), .Selection(alu_12_bit_3_sign_flag),
    .Output({mux_12_bit_1_output, Difference}));

  // Notes on the sheet:
  //   larger
  //   max shift 31
endmodule

// CMP_9
module Comparator_9_bit (
  input  [8:0] X,
  input  [8:0] Y,
  output [8:0] SMALLER,
  output X_Y,
  output [8:0] LARGER,
  output [4:0] DIFFERENCE
);

  wire alu_12_bit_3_sign_flag;
  wire [11:0] alu_12_bit_1_output, alu_12_bit_2_output;
  wire [11:5] mux_12_bit_1_output;

  ALU_12_bit alu_12_bit_1 (
    .Input_1({3'b000, X}), .Input_2({3'b000, Y}), .Control(2'b11), .Output(alu_12_bit_1_output),
    .Sign_Flag(X_Y));  // open: Carry_Out, Zero_Flag
  MUX_9_bit mux_9_bit_1 (.X(Y), .Y(X), .Selection(X_Y), .Output(SMALLER));
  MUX_9_bit mux_9_bit_2 (.X(X), .Y(Y), .Selection(X_Y), .Output(LARGER));
  ALU_12_bit alu_12_bit_2 (
    .Input_1(alu_12_bit_1_output), .Input_2({12{1'b0}}), .Control({1'b0, X_Y}), .Output(alu_12_bit_2_output));  // open: Carry_Out, Zero_Flag, Sign_Flag
  ALU_12_bit alu_12_bit_3 (
    .Input_1(alu_12_bit_2_output), .Input_2(12'h1f), .Control(2'b11), .Sign_Flag(alu_12_bit_3_sign_flag));  // open: Output, Carry_Out, Zero_Flag
  MUX_12_bit mux_12_bit_1 (
    .X(12'h1f), .Y(alu_12_bit_2_output), .Selection(alu_12_bit_3_sign_flag),
    .Output({mux_12_bit_1_output, DIFFERENCE}));

  // Notes on the sheet:
  //   larger
  //   max shift 31
endmodule

module main (
);

  Comparator_9_bit comparator_9_bit_1 ();  // open: X, Y, SMALLER, X_Y, LARGER, DIFFERENCE
  Comparator_With_Smaller_Fraction comparator_with_smaller_fraction_1 ();  // open: X_fraction, Y_fraction, X, Y, LargerFraction, SmallerFraction, X_Y, Common_Exponent, Difference
endmodule
