// Logisim project Floating_Point_Adder.circ as structural Verilog: 2 circuits, main circuit FPA
module FPA (
  input  [31:0] Input_2,
  input  [31:0] Input_1,
  output Overflow,
  output Underflow,
  output [31:0] Output,
  output NAN_Output,
  output INF_Output,
  output Denormalized_output
);

  wire and_1_out, comparator_1_eq, comparator_2_eq, comparator_with_smaller_fraction_1_x_y,
       input_validator_2_denormalized_input_1, multiplexer_1_out, multiplexer_2_out, n7486_1_p4, n74157_1_p4,
       nor_1_out, normalizer_1_denormalized, normalizer_1_overflow, normalizer_1_underflow, not_1_out,
       not_2_out;
  wire [4:0] comparator_with_smaller_fraction_1_difference;
  wire [8:0] comparator_with_smaller_fraction_1_common_exponent;
  wire [9:0] shifter_2_out;
  wire [31:0] comparator_with_smaller_fraction_1_largerfraction,
       comparator_with_smaller_fraction_1_smallerfraction, input_validator_1_valid_fraction_1,
       input_validator_1_valid_fraction_2, Manual_ALU_result, normalizer_1_normalized_fraction,
       Rounder_output, shifter_1_out;

  Comparator #(.width(32)) comparator_1 (.a(Input_1), .b(Input_2), .eq(comparator_1_eq));  // open: gt, lt
  Comparator #(.width(32)) comparator_2 (.a(Input_1), .b({32{1'b0}}), .eq(comparator_2_eq));  // open: gt, lt
  and and_1 (and_1_out, comparator_1_eq, comparator_2_eq);
  Multiplexer multiplexer_1 (
    .in0(Input_2[31]), .in1(Input_1[31]), .out(multiplexer_1_out),
    .sel(comparator_with_smaller_fraction_1_x_y), .en(1'b1));
  Multiplexer multiplexer_2 (
    .in0(Input_1[31]), .in1(Input_2[31]), .out(multiplexer_2_out),
    .sel(comparator_with_smaller_fraction_1_x_y), .en(1'b1));
  Input_Validator input_validator_1 (
    .Fraction_1({2'b01, Input_1[21:0], {8{1'b0}}}), .EXponent_1(Input_1[30:22]),
    .Fraction_2({2'b01, Input_2[21:0], {8{1'b0}}}), .EXponent_2(Input_2[30:22]),
    .Valid_Fraction_1(input_validator_1_valid_fraction_1),
    .Valid_Fraction_2(input_validator_1_valid_fraction_2));  // open: Denormalized_Input_1, Denormalized_Input_2, NaN_Input_1, NaN_Input_2, INF_Input_1, INF_Input_2
  Comparator_With_Smaller_Fraction comparator_with_smaller_fraction_1 (
    .X_fraction(input_validator_1_valid_fraction_1), .Y_fraction(input_validator_1_valid_fraction_2),
    .X(Input_1[30:22]), .Y(Input_2[30:22]),
    .LargerFraction(comparator_with_smaller_fraction_1_largerfraction),
    .SmallerFraction(comparator_with_smaller_fraction_1_smallerfraction),
    .X_Y(comparator_with_smaller_fraction_1_x_y),
    .Common_Exponent(comparator_with_smaller_fraction_1_common_exponent),
    .Difference(comparator_with_smaller_fraction_1_difference));
  Shifter #(.width(32), .shift("lr")) shifter_1 (
    .in(comparator_with_smaller_fraction_1_smallerfraction),
    .\dist (comparator_with_smaller_fraction_1_difference), .out(shifter_1_out));
  Manual_ALU Manual_ALU (
    .X(comparator_with_smaller_fraction_1_largerfraction), .Y(shifter_1_out), .SignBit1(multiplexer_2_out),
    .SignBit2(multiplexer_1_out), .Sign_of_Result(Output[31]), .Result(Manual_ALU_result));
  Normalizer normalizer_1 (
    .Fraction(Rounder_output), .Exponent(comparator_with_smaller_fraction_1_common_exponent),
    .Normalized_Fraction(normalizer_1_normalized_fraction), .Normalized_Exponent(Output[30:22]),
    .Overflow(normalizer_1_overflow), .Underflow(normalizer_1_underflow),
    .Denormalized(normalizer_1_denormalized));
  // _7486 7486_1: pin names not known; wires that end beside it: comparator_with_smaller_fraction_1_common_exponent, normalizer_1_overflow, normalizer_1_underflow, n7486_1_p4
  // _74157 74157_1: pin names not known; wires that end beside it: n7486_1_p4, normalizer_1_overflow, normalizer_1_overflow, n74157_1_p4, 1'b0
  and and_2 (Underflow, normalizer_1_underflow, not_1_out);
  not not_1 (not_1_out, input_validator_2_denormalized_input_1);
  Rounder Rounder (.Normalized_Input(Manual_ALU_result), .Output(Rounder_output));
  Shifter #(.width(32)) shifter_2 (
    .in(normalizer_1_normalized_fraction), .\dist (5'b00010), .out({Output[21:0], shifter_2_out}));
  not not_2 (not_2_out, and_1_out);
  and and_3 (Overflow, nor_1_out, n74157_1_p4);
  and and_4 (Denormalized_output, normalizer_1_denormalized, not_2_out);
  nor nor_1 (nor_1_out, INF_Output, NAN_Output);
  Input_Validator input_validator_2 (
    .Fraction_1({Output[21:0], shifter_2_out}), .EXponent_1(Output[30:22]),
    .Denormalized_Input_1(input_validator_2_denormalized_input_1), .NaN_Input_1(NAN_Output),
    .INF_Input_1(INF_Output));  // open: Fraction_2, EXponent_2, Denormalized_Input_2, NaN_Input_2, INF_Input_2, Valid_Fraction_1, Valid_Fraction_2

  // Other names for the same wires on the sheet: IN1IN2[31:0] = Input_2

  // Notes on the sheet:
  //   (Sign bit taken to compare)
  //   Implicit bit(1)
  //   (Input 2 > Input 1)
  //   (Sign bit taken to compare)
  //   (sign bit of larger)
  //   (Sing bit of smaller)
  //   (Sum: might be denormalized)
  //   Implicit bit (1)
  //   (Sign of the result)
  //   (Might be again denormalized)
endmodule

module main (
  input  [31:0] Input_1,
  input  [31:0] Input_2,
  output [31:0] Output,
  output Overflow,
  output Underflow,
  output NAN_Output,
  output Denormalized_Output,
  output INF_Output
);

  FPA fpa_1 (
    .Input_2(Input_1), .Input_1(Input_2), .Overflow(Overflow), .Underflow(Underflow), .Output(Output),
    .NAN_Output(NAN_Output), .INF_Output(INF_Output), .Denormalized_output(Denormalized_Output));
endmodule
