// Logisim project Normalizer.circ as structural Verilog: 2 circuits, main circuit main
module main (
);

  Normalizer normalizer_1 ();  // open: Fraction, Exponent, Normalized_Fraction, Normalized_Exponent, Overflow, Underflow, Denormalized
endmodule

module Normalizer (
  input  [31:0] Fraction,
  input  [8:0] Exponent,
  output [31:0] Normalized_Fraction,
  output [8:0] Normalized_Exponent,
  output Overflow,
  output Underflow,
  output Denormalized
);

  wire alu_16_bit_1_sign_flag, alu_16_bit_1_zero_flag, n7408_1_p3, priority_encoder_32x5_1_valid_bit,
       priority_encoder_32x5_2_valid_bit;
  wire [0:0] comparator_9_bit_1_x_y;
  wire [4:0] comparator_9_bit_1_difference, Difftunnel, priority_encoder_32x5_1_a0,
       priority_encoder_32x5_2_a0;
  wire [8:0] mux_9_bit_1_output, mux_9_bit_3_output;
  wire [15:0] alu_16_bit_1_output;
  wire [31:0] shifter_1_out, shifter_2_out, shifter_3_out, shifter_4_out;

  MUX_9_bit mux_9_bit_1 (
    .X({9{1'b0}}), .Y(9'h1e), .Selection(priority_encoder_32x5_1_valid_bit), .Output(mux_9_bit_1_output));
  Comparator_9_bit comparator_9_bit_1 (
    .X({4'b0000, priority_encoder_32x5_1_a0}), .Y(mux_9_bit_1_output), .X_Y(comparator_9_bit_1_x_y[0]),
    .DIFFERENCE(comparator_9_bit_1_difference));  // open: SMALLER, LARGER
  Priority_Encoder_32x5 priority_encoder_32x5_1 (
    .in_1(Fraction), .Valid_Bit(priority_encoder_32x5_1_valid_bit), .A4(priority_encoder_32x5_1_a0[4]),
    .A3(priority_encoder_32x5_1_a0[3]), .A2(priority_encoder_32x5_1_a0[2]),
    .A1(priority_encoder_32x5_1_a0[1]), .A0(priority_encoder_32x5_1_a0[0]));
  Shifter #(.width(32)) shifter_1 (.in(Fraction), .\dist (comparator_9_bit_1_difference), .out(shifter_1_out));
  Shifter #(.width(32), .shift("lr")) shifter_2 (
    .in(Fraction), .\dist (comparator_9_bit_1_difference), .out(shifter_2_out));
  Comparator #(.width(9)) comparator_1 (.a({4'b0000, Difftunnel}), .b(Exponent), .eq(Denormalized));  // open: gt, lt
  ALU_16_bit alu_16_bit_1 (
    .Input_1({{7{1'b0}}, Exponent}), .Input_2({{11{1'b0}}, comparator_9_bit_1_difference}),
    .Control({1'b1, comparator_9_bit_1_x_y[0]}), .Output(alu_16_bit_1_output),
    .Zero_Flag(alu_16_bit_1_zero_flag), .Sign_Flag(alu_16_bit_1_sign_flag));  // open: Carry_Out
  Shifter #(.width(32)) shifter_3 (.in(Fraction), .\dist (5'b00010), .out(shifter_3_out));
  MUX_32_bit mux_32_bit_1 (
    .X(shifter_2_out), .Y(shifter_1_out), .Selection(comparator_9_bit_1_x_y[0]), .Output(Normalized_Fraction));
  // _7408 7408_1: pin names not known; wires that end beside it: alu_16_bit_1_zero_flag, priority_encoder_32x5_1_valid_bit, n7408_1_p3, 1'b0, 1'b1
  Shifter #(.width(32), .shift("lr")) shifter_4 (.in(shifter_3_out), .\dist (5'b00010), .out(shifter_4_out));
  // _7432 7432_1: pin names not known; wires that end beside it: alu_16_bit_1_sign_flag, n7408_1_p3, Underflow, 1'b0, 1'b1
  MUX_9_bit mux_9_bit_2 (
    .X({9{1'b0}}), .Y(alu_16_bit_1_output[8:0]), .Selection(priority_encoder_32x5_1_valid_bit),
    .Output(Normalized_Exponent));
  ALU_16_bit alu_16_bit_2 (
    .Input_1(16'h1fe), .Input_2(alu_16_bit_1_output), .Control(2'b11), .Sign_Flag(Overflow));  // open: Output, Carry_Out, Zero_Flag
  MUX_9_bit mux_9_bit_3 (
    .X({9{1'b0}}), .Y(9'h1e), .Selection(priority_encoder_32x5_2_valid_bit), .Output(mux_9_bit_3_output));
  Comparator_9_bit comparator_9_bit_2 (
    .X({4'b0000, priority_encoder_32x5_2_a0}), .Y(mux_9_bit_3_output), .DIFFERENCE(Difftunnel));  // open: SMALLER, X_Y, LARGER
  Priority_Encoder_32x5 priority_encoder_32x5_2 (
    .in_1(shifter_4_out), .Valid_Bit(priority_encoder_32x5_2_valid_bit), .A4(priority_encoder_32x5_2_a0[4]),
    .A3(priority_encoder_32x5_2_a0[3]), .A2(priority_encoder_32x5_2_a0[2]),
    .A1(priority_encoder_32x5_2_a0[1]), .A0(priority_encoder_32x5_2_a0[0]));

  // Notes on the sheet:
  //   (V)
  //   (To get Where the 1 is)
  //   (Whether LS or RS)
  //   (LS)
  //   (RS)
  //   (V)
endmodule
