// Logisim project Rounder.circ as structural Verilog: 2 circuits, main circuit Rounder
module Rounder (
  input  [31:0] Normalized_Input,
  output [31:0] Output
);

  wire n7432_1_p3, n7432_1_p6;
  wire [0:0] n7408_1_p3;
  wire [31:24] _32_bit_ALU_output;

  // _7432 7432_1: pin names not known; wires that end beside it: Normalized_Input[6], Normalized_Input[7], n7432_1_p3, n7432_1_p3, Normalized_Input[9], n7432_1_p6, 1'b0, 1'b1
  // _7408 7408_1: pin names not known; wires that end beside it: n7432_1_p6, Normalized_Input[8], n7408_1_p3[0], 1'b0, 1'b1
  ALU_32_bit _32_bit_ALU (
    .Input_1({{8{1'b0}}, Normalized_Input[31:8]}), .Input_2({{31{1'b0}}, n7408_1_p3[0]}), .Control(2'b10),
    .Output({_32_bit_ALU_output, Output[31:8]}));  // open: Carry_Out, Zero_Flag, Sign_Flag

  assign Output[7:0] = {8{1'b0}};

  // Notes on the sheet:
  //   7  => G
  //   6  => R
  //   5  => S
  //   8  => L
  //   L
  //   (G)
  //   G && (R||S||L)
  //   (R||S||L)
endmodule

module main (
);

  Rounder rounder_1 ();  // open: Normalized_Input, Output
endmodule
